# Fritzing sketch fritzing circuit (saved by Fritzing 0.9.4)

parts:
  Part2 = Arduino Uno (Rev3)
  M6 = L293D Motor Driver
  M7 = DC Motor
  M8 = DC Motor
  M9 = DC Motor
  M10 = DC Motor
  BAT2 = BC9VPC [package=bc9vpc]
  e-radionica_com1 = LM393 LDR breakout [part_number=100027]
  e-radionica_com2 = LM393 LDR breakout [part_number=100027]

nets:
  N1: Part2.A0, e-radionica_com2.AO
  N2: Part2.A2, e-radionica_com1.AO
  N3: Part2.D9_PWM, M6.pin_5
  N4: Part2.D10_PWM/SS, M6.pin_6
  N5: Part2.D11_PWM/MOSI, M6.pin_7
  N6: Part2.D12/MISO, M6.pin_8
  VCC: Part2.5V, e-radionica_com1.VCC, e-radionica_com2.VCC
  GND: Part2.GND, BAT2.V-, e-radionica_com1.GND, e-radionica_com2.GND
  N7: Part2.VIN, BAT2.V+
  N8: M6.pin_9, M9.pin_1, M10.pin_1
  N9: M6.pin_10, M9.pin_2, M10.pin_2
  N10: M6.pin_11, M7.pin_1, M8.pin_1
  N11: M6.pin_12, M7.pin_2, M8.pin_2
